# Fritzing sketch mechane (saved by Fritzing 0.8.3b)
breadboards: 4

parts:
  CPU = atmega168 [package=dip]
  motor_driver = H-Bridge [package=THT]
  battery = LIPO-2000mAh [package=lipo-2000]
  3_3v_reg = V_REG_LD1117VXX [package=78xxl]
  isp_header = AVR_MINI_PROG [package=avr_mini_prog]
  radio = RFM12b HopeRF Transceiver
  defaults = Solder Jumper [package=sj_2s]
  status_(connection) = smd LED [color="Red (633nm)" package="0603 [SMD]"]
  reset = Solder Jumper [package=sj_2s]
  baud=9600 = Solder Jumper [package=sj_2s]
  status_(rx/tx) = smd LED [color="Red (633nm)" package="0603 [SMD]"]
  Bluetooth = RN-42 SMD [chip_label=IC package=QFN-32]
  encoder = Header 6 [package=molex-1x6_lock]
  R1 = Resistor [tolerance=±5% resistance=220 package=THT]
  R2 = Resistor [tolerance=±5% resistance=220 package=THT]
  R3 = Resistor [tolerance=±5% resistance=220 package=THT]
  Q1 = MOSFET-NCHANNEL [package=sot23-3]
  RRIGHT = Resistor [tolerance=±5% resistance=10k package="0603 [SMD]"]
  RTOP = Resistor [tolerance=±5% resistance=10k package="0603 [SMD]"]
  RLEFT = Resistor [tolerance=±5% resistance=10k package="0603 [SMD]"]
  RBOT = Resistor [tolerance=±5% resistance=10k package="0603 [SMD]"]
  U1 = Voltage Regulator - 5V [package="DPak [SMD]"]

nets:
  reset: CPU.RESET, isp_header.RST
  N1: CPU.D0_(RX), Bluetooth.UART_TX
  N2: CPU.D1_(TX), Bluetooth.UART_RX
  N3: CPU.D2, radio.2_nIRQ
  N4: CPU.D3_(PWM), radio.14_nSEL
  3.3v: CPU.VCC, CPU.AVCC, motor_driver.VCC1, 3_3v_reg.OUT, radio.3_FSK/DATA, radio.9_VDD, defaults.2, baud=9600.2, Bluetooth.VDD, encoder.4, U1.output_voltage
  GND: CPU.GND, motor_driver.GND1, motor_driver.GND2, motor_driver.GND3, motor_driver.GND4, battery.-, 3_3v_reg.GND, isp_header.GND, radio.7_GND, radio.10_GND, status_(connection).anode, reset.2, status_(rx/tx).cathode, Bluetooth.GND, encoder.3, R1.Pin_0, R2.Pin_0, R3.Pin_0, RBOT.Pin_1, U1.GND
  N5: CPU.D5_(PWM), motor_driver.1A, motor_driver.4A, R1.Pin_1
  N6: CPU.D6_(PWM), motor_driver.2A, motor_driver.3A, R2.Pin_1
  N7: CPU.D8, encoder.6
  N8: CPU.D9_(PWM), encoder.5
  mosi: CPU.D11_(PWM), isp_header.MOSI, radio.12_SDI
  miso: CPU.D12, isp_header.MISO, radio.1_SDO
  sck: CPU.D13, isp_header.SCK, radio.13_SCK
  N9: CPU.A0, motor_driver.1_2EN, motor_driver.3_4EN, R3.Pin_1
  N10: motor_driver.1Y, motor_driver.4Y, encoder.1
  N11: motor_driver.2Y, motor_driver.3Y, encoder.2
  batt: motor_driver.VCC2, battery.+, 3_3v_reg.IN, U1.input_voltage
  N12: defaults.1, Bluetooth.PIO4
  N13: status_(connection).cathode, Bluetooth.PIO2
  N14: reset.1, Bluetooth.RESET
  N15: baud=9600.1, Bluetooth.PIO7
  N16: status_(rx/tx).anode, Bluetooth.PIO8
  LV: Q1.G, RLEFT.Pin_0
  TX_LV: Q1.S, RLEFT.Pin_1
  TX_HV: Q1.D, RRIGHT.Pin_1
  HV: RRIGHT.Pin_0
  RX_HV: RTOP.Pin_0
  RX_LV: RTOP.Pin_1, RBOT.Pin_0

custom parts:
  RFM12b HopeRF Transceiver: RF Transceiver by Hope RF. Well supported Arduino libraries are available. Part is available in several frequencies (433MHz, 915MHz)...
  RN-42 SMD: This is the surface mount RN-42 part
