# Fritzing sketch mechane_perf_v1 (saved by Fritzing 0.8.3b)
perfboards: 2

parts:
  U1 = atmega328 [package=dip]
  IC1 = H-Bridge [package=THT]
  RFM12b1 = RFM12b HopeRF Transceiver
  Q1 = NPN-Transistor [package="TO92 [THT]"]
  Q2 = NPN-Transistor [package="TO92 [THT]"]
  Q3 = NPN-Transistor [package="TO92 [THT]"]
  R4 = Resistor [tolerance=±5% resistance=10k package=THT]
  R5 = Resistor [tolerance=±5% resistance=10k package=THT]
  R6 = Resistor [tolerance=±5% resistance=10k package=THT]
  R7 = Resistor [tolerance=±5% resistance=1k package=THT]
  R8 = Resistor [tolerance=±5% resistance=1k package=THT]
  R9 = Resistor [tolerance=±5% resistance=1k package=THT]
  J1 = male pin header, 6 pins [form="♂ (male)"]
  U2 = Voltage Regulator - 5V [package="TO220 [THT]"]
  U5 = V_REG_LD1117VXX [package=78xxl]
  J2 = male pin header, 3 pins [form="♂ (male)"]

nets:
  N1: U1.D0_(RX), J2.pin3
  N2: U1.D1_(TX), J2.pin2
  N3: U1.D3_(PWM), RFM12b1.2_nIRQ
  3.3v: U1.VCC, U1.AVCC, RFM12b1.9_VDD, J1.pin3, U5.OUT
  GND: U1.GND, IC1.GND1, IC1.GND2, IC1.GND3, IC1.GND4, RFM12b1.7_GND, RFM12b1.10_GND, Q1.E, Q2.E, Q3.E, J1.pin4, U2.GND, U5.GND, J2.pin1
  N4: U1.D5_(PWM), R8.Pin_1
  N5: U1.D6_(PWM), R9.Pin_1
  N6: U1.D7, R7.Pin_0
  N7: U1.D8, J1.pin1
  N8: U1.D9_(PWM), J1.pin2
  N9: U1.D10_(PWM), RFM12b1.14_nSEL
  N10: U1.D11_(PWM), RFM12b1.12_SDI
  N11: U1.D12, RFM12b1.1_SDO
  N12: U1.D13, RFM12b1.13_SCK
  N13: IC1.1_2EN, Q3.C, R4.Pin_0
  N14: IC1.1A, Q1.C, R5.Pin_0
  N15: IC1.1Y, J1.pin6
  N16: IC1.2Y, J1.pin5
  N17: IC1.2A, Q2.C, R6.Pin_0
  12v: IC1.VCC2, U2.input_voltage, U5.IN
  5v: IC1.VCC1, R4.Pin_1, R5.Pin_1, R6.Pin_1, U2.output_voltage
  N18: Q1.B, R8.Pin_0
  N19: Q2.B, R9.Pin_0
  N20: Q3.B, R7.Pin_1

custom parts:
  RFM12b HopeRF Transceiver: RF Transceiver by Hope RF. Well supported Arduino libraries are available. Part is available in several frequencies (433MHz, 915MHz)...
